# Fritzing sketch Shematic (saved by Fritzing 0.9.3b)
breadboards: 1

parts:
  Part1 = Arduino Uno (Rev3)
  part = LCD-16X2 [package=lcd-16x2_noholes]
  R1 = Trimmer Potentiometer [maximum_resistance=10kΩ package=THT]
  ultrasonic_sensor = SRF05 Ultrasonic Rangefinder

nets:
  N1: Part1.D8, ultrasonic_sensor.Echo
  N2: Part1.D9_PWM, ultrasonic_sensor.Trig
  N3: Part1.D11_PWM/MOSI, part.E
  N4: Part1.D12/MISO, part.RS
  N5: Part1.GND, part.R_W, part.K, R1.wiper
  N6: Part1.D2, part.DB7
  N7: Part1.D3_PWM, part.DB6
  N8: Part1.D4, part.DB5
  N9: Part1.D5_PWM, part.DB4
  N10: Part1.5V, R1.leg1
  VSS: part.VSS, ultrasonic_sensor.GND
  VDD: part.VDD, part.A, ultrasonic_sensor.VCC
  N11: part.VO, R1.leg2
